# Fritzing sketch receiver (saved by Fritzing 0.9.2b)

parts:
  IR1_1838B = TSOP312.., 314.. [package=THT]
  Part2 = Arduino Uno (Rev3) - ICSP

nets:
  GND: IR1_1838B.GND, Part2.GND
  3.3V: IR1_1838B.Vs, Part2.5V
  N1: IR1_1838B.Data, Part2.D2
