# Fritzing sketch arduino-pins (saved by Fritzing 0.9.2b)

parts:
  R1 = Resistor [tolerance=±20% resistance=10 package="2512 [SMD]"]
  Part2 = Arduino Uno (Rev3)

nets:
  N1: R1.Pin_1, Part2.D13/SCK

notes:
  to Wii-mote
  to Play Station Controller
  data
  gnd
  clock
  vcc
  command
